# Fritzing sketch schematic (saved by Fritzing 0.9.3b)

parts:
  8x8_LED_matrix_MAX1 = 8x8 Red 8x8 LED Matrix with MAX7219
  Raspberry_Pi_1 = Raspberry Pi 3 [part_number=RPI-3-V1.2]

nets:
  VCC: 8x8_LED_matrix_MAX1.VCC, 8x8_LED_matrix_MAX1.VCC_PT, Raspberry_Pi_1.5V
  GND: 8x8_LED_matrix_MAX1.GND, 8x8_LED_matrix_MAX1.CLK_PT, Raspberry_Pi_1.GND
  N1: 8x8_LED_matrix_MAX1.DIN, Raspberry_Pi_1.GIPO10
  N2: 8x8_LED_matrix_MAX1.DIN_CHN, 8x8_LED_matrix_MAX1.CS, Raspberry_Pi_1.GIPO8
  N3: 8x8_LED_matrix_MAX1.CLK, Raspberry_Pi_1.GIPO11

custom parts:
  8x8 Red 8x8 LED Matrix with MAX7219: Description: 8 by 8 red LED matrix with a MAX7219 controller.
